// Logisim project ALU_01bit_Task01.circ as structural Verilog: 1 circuit, main circuit main
module main (
  input  carry_in,
  input  b_invert,
  input  [1:0] in_3,
  input  A,
  input  B,
  input  Less,
  output Result,
  output out_8,
  output set
);

  wire AND_out, multiplexer_1_out, not_1_out, OR_out;

  not not_1 (not_1_out, B);
  Multiplexer #(.enable("false")) multiplexer_1 (.in0(B), .in1(not_1_out), .out(multiplexer_1_out), .sel(b_invert));
  and AND (AND_out, A, multiplexer_1_out);
  or OR (OR_out, A, multiplexer_1_out);
  Adder #(.width(1)) adder_1 (.a(A), .b(multiplexer_1_out), .out(set), .cin(carry_in), .cout(out_8));
  Multiplexer #(.select(2), .enable("false")) multiplexer_2 (
    .in0(AND_out), .in1(OR_out), .in2(set), .in3(Less), .out(Result), .sel(in_3));

  // Notes on the sheet:
  //           B_not
  //        B_out
endmodule
