// Logisim project ALU_32Bit.circ as structural Verilog: 1 circuit, main circuit main
module main (
  input  [31:0] A,
  input  [3:0] alu_op,
  input  [31:0] B,
  output [31:0] Result,
  output zero_flag
);

  wire comparator_1_lt, comparator_2_lt;
  wire [31:0] adder_1_out, AND_out, bit_extender_1_out, bit_extender_2_out, OR_out, shifter_1_out,
       shifter_2_out, shifter_3_out, subtractor_1_out, XOR_out;

  Adder #(.width(32)) adder_1 (.a(A), .b(B), .out(adder_1_out));  // open: cin, cout
  Subtractor #(.width(32)) subtractor_1 (.a(A), .b(B), .out(subtractor_1_out));  // open: bin, bout
  assign AND_out = A & B;  // AND_Gate AND, 32 bits wide
  assign OR_out = A | B;  // OR_Gate OR, 32 bits wide
  assign XOR_out = A ^ B;  // XOR_Gate XOR, 32 bits wide
  Comparator #(.width(32), .mode("unsigned")) comparator_1 (.a(A), .b(B), .lt(comparator_1_lt));  // open: gt, eq
  assign bit_extender_1_out = {{31{1'b0}}, comparator_1_lt};  // Bit_Extender bit_extender_1
  Comparator #(.width(32)) comparator_2 (.a(A), .b(B), .lt(comparator_2_lt));  // open: gt, eq
  assign bit_extender_2_out = {{31{1'b0}}, comparator_2_lt};  // Bit_Extender bit_extender_2
  Shifter #(.width(32)) shifter_1 (.in(A), .\dist (B[4:0]), .out(shifter_1_out));
  Shifter #(.width(32), .shift("lr")) shifter_2 (.in(A), .\dist (B[4:0]), .out(shifter_2_out));
  Shifter #(.width(32), .shift("ar")) shifter_3 (.in(A), .\dist (B[4:0]), .out(shifter_3_out));
  Multiplexer #(.select(4), .width(32), .enable("false")) multiplexer_1 (
    .in0(adder_1_out), .in1(subtractor_1_out), .in2(AND_out), .in3(OR_out), .in4(XOR_out),
    .in5(bit_extender_1_out), .in6(bit_extender_2_out), .in7(shifter_1_out), .in8(shifter_2_out),
    .in9(shifter_3_out), .out(Result), .sel(alu_op));  // open: in10, in11, in12, in13, in14, in15
  Comparator #(.width(32), .mode("unsigned")) comparator_3 (
    .a(Result), .b({32{1'b0}}), .eq(zero_flag));  // open: gt, lt

  // Notes on the sheet:
  //   splitter
  //     ADD
  //   SUB
  //       STLU
  //      STL 
  //        SLL
  //   SRL
  //   SRA
endmodule
