// Logisim project task02_STL_4bit ALU.circ as structural Verilog: 2 circuits, main circuit main
module main (
  input  carry_in,
  input  b_invert,
  input  [1:0] in_3,
  input  A,
  input  B,
  input  Less,
  output Result,
  output out_8,
  output set
);

  wire AND_out, multiplexer_1_out, not_1_out, OR_out;

  not not_1 (not_1_out, B);
  Multiplexer #(.enable("false")) multiplexer_1 (.in0(B), .in1(not_1_out), .out(multiplexer_1_out), .sel(b_invert));
  and AND (AND_out, A, multiplexer_1_out);
  or OR (OR_out, A, multiplexer_1_out);
  Adder #(.width(1)) adder_1 (.a(A), .b(multiplexer_1_out), .out(set), .cin(carry_in), .cout(out_8));
  Multiplexer #(.select(2), .enable("false")) multiplexer_2 (
    .in0(AND_out), .in1(OR_out), .in2(set), .in3(Less), .out(Result), .sel(in_3));

  // Notes on the sheet:
  //           B_not
  //        B_out
endmodule

module _4Bit_ALU (
  input  [3:0] A,
  input  in_2,
  input  [1:0] in_3,
  input  [3:0] B,
  output [3:0] Result,
  output Zero_Flag,
  output out_7,
  output Overflow_Flag,
  output Carry_Flag
);

  wire main_1_out_8, main_2_out_8, main_3_out_8, main_4_set;

  main main_1 (
    .carry_in(in_2), .A(A[0]), .B(B[0]), .Less(main_4_set), .Result(Result[0]), .b_invert(in_2), .in_3(in_3),
    .out_8(main_1_out_8));  // open: set
  main main_2 (
    .carry_in(main_1_out_8), .A(A[1]), .B(B[1]), .Less(1'b0), .Result(Result[1]), .b_invert(in_2),
    .in_3(in_3), .out_8(main_2_out_8));  // open: set
  main main_3 (
    .carry_in(main_2_out_8), .A(A[2]), .B(B[2]), .Less(1'b0), .Result(Result[2]), .b_invert(in_2),
    .in_3(in_3), .out_8(main_3_out_8));  // open: set
  main main_4 (
    .carry_in(main_3_out_8), .A(A[3]), .B(B[3]), .Less(1'b0), .Result(out_7), .b_invert(in_2), .in_3(in_3),
    .out_8(Carry_Flag), .set(main_4_set));
  nor nor_1 (Zero_Flag, Result[0], Result[1], Result[2], out_7);
  xor XOR (Overflow_Flag, main_3_out_8, Carry_Flag);

  assign Result[3] = out_7;

  // Notes on the sheet:
  //                 Sign_Flag
endmodule
